# Fritzing sketch HelloWitch (saved by Fritzing 0.9.3b)
circuit board: 9.44245cm x 7.90416cm
breadboards: 1

parts:
  Part2 = Arduino Nano (Rev3.0)
  U1 = LIPO-2000mAh [package=lipo-2000]
  DFRobot_DFPlayer_Mini1 = DFRobot DFPlayer Mini [part_number=DFR0299]
  SP1 = SPEAKER [package=pcb_mount_speaker]
  PIR1 = PIR sensor
  Sensor1 = TTP223B Capacitive Touch Sensor Module
  R4 = Resistor [tolerance=±5% resistance=47 package="0603 [SMD]"]
  R2 = Resistor [tolerance=±5% resistance=47 package="0603 [SMD]"]
  R1 = Resistor [tolerance=±5% resistance=1k package="0603 [SMD]"]
  J1 = Basic Servo
  LED5 = LED - 5mm [color="Green (565nm)" package="5 mm [THT]"]
  LED6 = LED - 5mm [color="Blue (430nm)" package="5 mm [THT]"]
  LED7 = LED - 5mm [color="Orange (620nm)" package="5 mm [THT]"]
  R3 = Resistor [tolerance=±5% resistance=47 package="0603 [SMD]"]

nets:
  GND: Part2.GND, U1.-, DFRobot_DFPlayer_Mini1.GND-1, DFRobot_DFPlayer_Mini1.GND-2, PIR1.GND, Sensor1.GND, J1.gnd, LED5.anode, LED6.anode, LED7.anode
  N1: Part2.D3, R4.Pin_0
  N2: Part2.D4, R2.Pin_0
  N3: Part2.D5, R3.Pin_0
  N4: Part2.D7, PIR1.SIG
  N5: Part2.D8, Sensor1.SIG
  N6: Part2.D9, J1.pulse
  N7: Part2.D10, DFRobot_DFPlayer_Mini1.TX
  N8: Part2.D11/MOSI, R1.Pin_1
  VIN: Part2.VIN, U1.+, J1.vcc
  VCC: Part2.5V, DFRobot_DFPlayer_Mini1.VCC, PIR1.VDD, Sensor1.VCC
  N9: DFRobot_DFPlayer_Mini1.RX, R1.Pin_0
  N10: DFRobot_DFPlayer_Mini1.SPK_1, SP1.-
  N11: DFRobot_DFPlayer_Mini1.SPK_2, SP1.+
  N12: R4.Pin_1, LED5.cathode
  N13: R2.Pin_1, LED7.cathode
  N14: LED6.cathode, R3.Pin_1

notes:
  4 pin Orange system
  3 pin Green eyes
  5 pin Blue lantern
  Start sequnce

custom parts:
  TTP223B Capacitive Touch Sensor Module: The TTP223B capacitive touch sensor module uses the TTP223B IC. The appropriate voltage is approximately 2 to 5.5 volts.

// code stored in the sketch: LedFade.ino
#include "fade.h"
#include "MP3Player.h"
#include "BlinkLed.h"
#include "ServoController.h"

//Pins

#define LANTERN_PIN 3
#define TEST_PIN 4
#define EYES_PIN 5

#define MOTION_SENSOR_PIN  7


#define BTN_PLAY 8

#define MP3_RX 10
#define MP3_TX 11
#define SERVO_PIN 9

// seconds
int MOVING_TIME = 15;
int SLEEPING_TIME = 30; 
int SOUND_TIME = 2;

unsigned long move_start_ms;
unsigned long blink_start_ms;

int state = 0; 

//Classes
FadeLED* eyesFade;
FadeLED* lanternFade;
BlinkLED* testBlink;
ServoController* servo;

MP3Player* mp3Plyer;

void setup() {
  //Serial.begin(9600);  

  eyesFade = new FadeLED(EYES_PIN,0.5);
  lanternFade = new FadeLED(LANTERN_PIN,2.0);
  testBlink = new BlinkLED(TEST_PIN, 3000, 200);
  servo = new ServoController(SERVO_PIN);

  pinMode(BTN_PLAY, INPUT);
  pinMode(TEST_PIN, OUTPUT);
  pinMode(MOTION_SENSOR_PIN, INPUT);

  digitalWrite(TEST_PIN, LOW);

  mp3Plyer = new MP3Player(MP3_RX, MP3_TX);
  mp3Plyer->setVolume(5);


  for(int  i = 0; i < 15; i++) {
    //Serial.print(".");
    delay(950);
    digitalWrite(TEST_PIN, HIGH);
    delay(50);
    digitalWrite(TEST_PIN, LOW);
  }
  
  //Serial.println("Ready");
  move_start_ms = millis();
}

void loop() 
{
  unsigned long timeout = millis() - move_start_ms;

  if (state == 0) 
  {
    if (wakeUp())
    {
      state = 1;
      digitalWrite(TEST_PIN, HIGH);
      
      //mp3Plyer->reset();
      delay(100);
      mp3Plyer->play();
      delay(100);
      move_start_ms = millis();
      return;
    }
    testBlink->update();

    delay(100);
    return;
  }

  updateFades();
  updateServo();

  delay(1);
  if (timeout <= MOVING_TIME * 1000) {
    return; 
  }
  move_start_ms = millis();

  if (state == 1)
  {
    state = 2;
    return;
  }

  digitalWrite(TEST_PIN, LOW);
  state = 0;
  delay(10);
  blink_start_ms = millis() + 3000;
  testBlink->reset();
}

void updateFades() 
{
  eyesFade->update(state);
  lanternFade->update(state);
}

void updateServo()
{
  servo->update(state);
}

bool wakeUp() 
{
  return digitalRead(MOTION_SENSOR_PIN) == HIGH || digitalRead(BTN_PLAY) == HIGH;
  //int pinState = digitalRead(BTN_PLAY) == HIGH;
  //int pinState = digitalRead(MOTION_SENSOR_PIN);
  //Serial.print("Sensor: ");
  //Serial.println(pinState);
  //return pinState == HIGH;
}
